# Fritzing sketch ElBanquos_1D_pong_mk1 (saved by Fritzing 0.9.3b)
breadboards: 1

parts:
  Bauteil2 = 12 NeoPixel Ring [part_number=1643]
  SP1 = SPEAKER [package=pcb_mount_speaker]
  R1 = Resistor [tolerance=±5% resistance=220 package=THT]
  Button_B = Pushbutton [package="[THT]"]
  Button_A = Pushbutton [package="[THT]"]
  Bauteil3 = Arduino Uno (Rev3)
  J1 = Screw terminal - 2 pins [package=THT]

nets:
  N1: Bauteil2.IN, Bauteil3.D7
  VDD: Bauteil2.VDD, Bauteil3.5V
  GND: Bauteil2.GND, R1.Pin_0, Button_B.Pin_1, Button_B.Pin_2, Button_A.Pin_1, Button_A.Pin_2, Bauteil3.GND
  N2: SP1.+, R1.Pin_1, J1.pin1
  N3: SP1.-, Bauteil3.D11_PWM/MOSI, J1.pin2
  N4: Button_B.Pin_3, Button_B.Pin_4, Bauteil3.D6_PWM
  N5: Button_A.Pin_3, Button_A.Pin_4, Bauteil3.D8

custom parts:
  12 NeoPixel Ring: 12 ultra bright smart LED NeoPixels are arranged in a circle with 1.5" (37mm) outer diameter. The rings are 'chainable' - connect the output pin of one to the input pin of another. Use only one microcontroller pin to control as many as you can chain together! Each LED is addressable as the driver chip is inside the LED. Each one has ~18mA constant current drive so the color will be very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
